# Fritzing sketch analogIn (saved by Fritzing 0.8.7b)
breadboards: 1

parts:
  BeagleBone1 = BeagleBone Black
  R1 = Rotary Potentiometer (Small) [maximum_resistance=100kΩ package=THT]

nets:
  N1: BeagleBone1.no_name_yet#32, R1.leg2
  N2: BeagleBone1.no_name_yet#34, R1.leg1
  N3: BeagleBone1.no_name_yet#36, R1.wiper

notes:
  +
  -

custom parts:
  BeagleBone Black: BeagleBone Black rev. A5B
