# Fritzing sketch flexResistor (saved by Fritzing 0.8.7b)
breadboards: 1

parts:
  BeagleBone1 = BeagleBone Black
  R1 = Basic Flex Resistor
  R2 = Resistor [tolerance=±10% resistance=22k package=THT]

nets:
  N1: BeagleBone1.no_name_yet#1, BeagleBone1.no_name_yet#34, R2.Pin_1
  N2: BeagleBone1.no_name_yet#32, R1.Pin_2
  N3: BeagleBone1.no_name_yet#36, R1.pin_1, R2.Pin_0

notes:
  +
  -
  P9
  P8

custom parts:
  BeagleBone Black: BeagleBone Black rev. A5B
