# Fritzing sketch i2cTemp (saved by Fritzing 0.8.7b)
breadboards: 1

parts:
  BeagleBone1 = BeagleBone Black
  U1 = TMP102 [package=sot563]
  R1 = Resistor [tolerance=±5% resistance=4.7k package=THT]
  R2 = Resistor [tolerance=±5% resistance=4.7k package=THT]

nets:
  N1: BeagleBone1.no_name_yet#1, U1.GND
  N2: BeagleBone1.no_name_yet#3, U1.ADD0, U1.VCC, R1.Pin_1, R2.Pin_1
  N3: BeagleBone1.no_name_yet#19, U1.SCL, R2.Pin_0
  N4: BeagleBone1.no_name_yet#20, U1.SDA, R1.Pin_0

notes:
  +
  -
  P9
  P8

custom parts:
  BeagleBone Black: BeagleBone Black rev. A5B
