# Fritzing sketch pushbuttonPullup (saved by Fritzing 0.8.7b)
breadboards: 1

parts:
  BeagleBone1 = BeagleBone Black
  S1 = Pushbutton [package="[THT]"]
  S2 = Pushbutton [package="[THT]"]

nets:
  N1: BeagleBone1.no_name_yet#1, S2.Pin_3, S2.Pin_4
  N2: BeagleBone1.no_name_yet#3, S1.Pin_3, S1.Pin_4
  N3: BeagleBone1.no_name_yet#26, S2.Pin_1, S2.Pin_2
  N4: BeagleBone1.no_name_yet#42, S1.Pin_1, S1.Pin_2

notes:
  +
  -

custom parts:
  BeagleBone Black: BeagleBone Black rev. A5B
