# Fritzing sketch rotaryEncoder (saved by Fritzing 0.8.7b)
breadboards: 1

parts:
  BeagleBone1 = BeagleBone Black
  ENCODER1 = Rotary Encoder with Knob

nets:
  N1: BeagleBone1.no_name_yet#1, ENCODER1.no_name_yet#2
  N2: BeagleBone1.no_name_yet#111, ENCODER1.no_name_yet#3
  N3: BeagleBone1.no_name_yet#112, ENCODER1.no_name_yet#1

notes:
  +
  -
  P9
  P8

custom parts:
  BeagleBone Black: BeagleBone Black rev. A5B
  Rotary Encoder with Knob: Rotary Encoder with 1/4" Shaft and Knob
