# Fritzing sketch GPS (saved by Fritzing 0.8.7b)
breadboards: 1

parts:
  BeagleBone1 = BeagleBone Black
  GPS1 = Adafruit Ultimate GPS Breakout

nets:
  N1: BeagleBone1.no_name_yet#1, GPS1.GND
  N2: BeagleBone1.no_name_yet#3, GPS1.3.3V
  N3: BeagleBone1.no_name_yet#11, GPS1.TX

custom parts:
  BeagleBone Black: BeagleBone Black rev. A5B
