# Fritzing sketch hc-sr04-ultraSonic (saved by Fritzing 0.8.7b)
breadboards: 1

parts:
  BeagleBone1 = BeagleBone Black
  Part1 = SRF05 Ultrasonic Rangefinder  # not connected
  R1 = Resistor [tolerance=±10% resistance=10k package=THT]
  R2 = Resistor [tolerance=±5% resistance=20k package=THT]

nets:
  N1: BeagleBone1.no_name_yet#1, R2.Pin_1
  N2: BeagleBone1.no_name_yet#41, R1.Pin_1, R2.Pin_0

notes:
  +
  -
  P9
  P8

custom parts:
  BeagleBone Black: BeagleBone Black rev. A5B
