# Fritzing sketch matrix16x24 (saved by Fritzing 0.8.7b)
breadboards: 1

parts:
  BeagleBone1 = BeagleBone Black
  U1 = AVR 10-pin ICSP Header [package=2x5-shrouded_smd]

nets:
  N1: BeagleBone1.no_name_yet#1, U1.5, U1.6
  N2: BeagleBone1.no_name_yet#3, U1.9, U1.10
  N3: BeagleBone1.no_name_yet#12, BeagleBone1.no_name_yet#23, U1.3, U1.4
  N4: BeagleBone1.no_name_yet#15, U1.7, U1.8
  N5: U1.1, U1.2

notes:
  +
  -
  P9
  P8

custom parts:
  BeagleBone Black: BeagleBone Black rev. A5B
