# Fritzing sketch neoPixel (saved by Fritzing 0.9.0b)
breadboards: 1

parts:
  BeagleBone1 = BeagleBone Black
  NEOPIXEL1 = Neopixel Strip -- White (60/m)

nets:
  N1: BeagleBone1.no_name_yet#1, NEOPIXEL1.GND
  N2: BeagleBone1.no_name_yet#3, NEOPIXEL1.DI
  N3: BeagleBone1.no_name_yet#132, NEOPIXEL1.+5V

notes:
  +
  -
  P9
  P8

custom parts:
  BeagleBone Black: BeagleBone Black rev. A5B
  Neopixel Strip -- White (60/m): Neopixel Strip, White, 60 pixels per meter.
