# Fritzing sketch ws2801 (saved by Fritzing 0.8.7b)
breadboards: 1

parts:
  BeagleBone1 = BeagleBone Black
  U1 = WS2801 [package=sop-14]

nets:
  N1: BeagleBone1.no_name_yet#1, U1.GND
  N2: BeagleBone1.no_name_yet#3, U1.VCC
  N3: BeagleBone1.no_name_yet#18, U1.SDI
  N4: BeagleBone1.no_name_yet#22, U1.CKI

notes:
  +
  -
  P9
  P8

custom parts:
  BeagleBone Black: BeagleBone Black rev. A5B
