# Fritzing sketch externLED (saved by Fritzing 0.8.7b)
breadboards: 1

parts:
  BeagleBone1 = BeagleBone Black
  LED1 = LED - 5mm [color="Red (633nm)" package="5 mm [THT]"]
  R1 = Resistor [tolerance=±5% resistance=220 package=THT]

nets:
  N1: BeagleBone1.no_name_yet#1, R1.Pin_1
  N2: BeagleBone1.no_name_yet#14, LED1.anode
  N3: LED1.cathode, R1.Pin_0

custom parts:
  BeagleBone Black: BeagleBone Black rev. A5B
