# Fritzing sketch i2cMatrix (saved by Fritzing 0.8.7b)
breadboards: 1

parts:
  BeagleBone1 = BeagleBone Black
  R1 = Resistor [tolerance=±5% resistance=4.7k package=THT]
  R2 = Resistor [tolerance=±5% resistance=4.7k package=THT]
  LED1 = 8x8 LED Matrix (blue)

nets:
  N1: BeagleBone1.no_name_yet#1, LED1.-
  N2: BeagleBone1.no_name_yet#3, R1.Pin_1, R2.Pin_1, LED1.+
  N3: BeagleBone1.no_name_yet#19, R2.Pin_0, LED1.C
  N4: BeagleBone1.no_name_yet#20, R1.Pin_0, LED1.D

notes:
  +
  -
  P9
  P8

custom parts:
  BeagleBone Black: BeagleBone Black rev. A5B
  8x8 LED Matrix (blue): 8x8 LED Matrix with I2C control (blue)
