# Fritzing sketch i2cMatrixLevelTrans (saved by Fritzing 0.8.7b)
breadboards: 1

parts:
  BeagleBone1 = BeagleBone Black
  R1 = Resistor [tolerance=±5% resistance=4.7k package=THT]
  U2 = PCA9306 [package=psop-8]
  LED1 = 8x8 LED Matrix (blue)  # not connected
  R2 = Resistor [tolerance=±5% resistance=4.7k package=THT]

nets:
  N1: BeagleBone1.no_name_yet#1, U2.VREF1
  N2: BeagleBone1.no_name_yet#3, R1.Pin_1, U2.SCL1, U2.VREF2, R2.Pin_1
  N3: BeagleBone1.no_name_yet#7, U2.EN
  N4: BeagleBone1.no_name_yet#19, U2.SDA1, R2.Pin_0
  N5: BeagleBone1.no_name_yet#20, R1.Pin_0, U2.GND

notes:
  +
  -
  P9
  P8

custom parts:
  BeagleBone Black: BeagleBone Black rev. A5B
  8x8 LED Matrix (blue): 8x8 LED Matrix with I2C control (blue)
