# Fritzing sketch i2cMatrixOLD (saved by Fritzing 0.8.7b)
breadboards: 1

parts:
  BeagleBone1 = BeagleBone Black
  U1 = TMP102 [package=sot563]
  R1 = Resistor [tolerance=±5% resistance=4.7k package=THT]
  R2 = Resistor [tolerance=±5% resistance=4.7k package=THT]
  U2 = PCA9306 [package=psop-8]
  LED1 = 8x8 LED Matrix (blue)

nets:
  N1: BeagleBone1.no_name_yet#1, U1.GND, U2.VREF1, LED1.-
  N2: BeagleBone1.no_name_yet#3, U1.ADD0, U1.VCC, R1.Pin_1, R2.Pin_1, U2.SCL1, U2.EN
  N3: BeagleBone1.no_name_yet#7, U2.VREF2, LED1.+
  N4: BeagleBone1.no_name_yet#19, U1.SCL, R2.Pin_0, U2.SDA1
  N5: BeagleBone1.no_name_yet#20, U1.SDA, R1.Pin_0, U2.GND
  N6: U2.SDA2, LED1.D
  N7: U2.SCL2, LED1.C

notes:
  +
  -
  P9
  P8

custom parts:
  BeagleBone Black: BeagleBone Black rev. A5B
  8x8 LED Matrix (blue): 8x8 LED Matrix with I2C control (blue)
