# Fritzing sketch neoPixelMatrix (saved by Fritzing 0.9.0b)

parts:
  BeagleBone1 = BeagleBone Black
  NEOPIXEL2 = Neopixel 8x8 Matrix

nets:
  N1: BeagleBone1.no_name_yet#1, NEOPIXEL2.GND
  N2: BeagleBone1.no_name_yet#3, NEOPIXEL2.VCC
  N3: BeagleBone1.no_name_yet#130, NEOPIXEL2.DIN

notes:
  P9
  P8

custom parts:
  BeagleBone Black: BeagleBone Black rev. A5B
  Neopixel 8x8 Matrix: Adafruit Neopixel 8x8 Matrix
