# Fritzing sketch powerSwitch (saved by Fritzing 0.8.7b)

parts:
  BeagleBone1 = BeagleBone Black
  SW1 = PowerSwitch Tail II

nets:
  N1: BeagleBone1.no_name_yet#3, SW1.+in
  N2: BeagleBone1.no_name_yet#14, SW1.-in

notes:
  +
  -
  P9
  P8

custom parts:
  BeagleBone Black: BeagleBone Black rev. A5B
