# Fritzing sketch bipolarStepperMotor (saved by Fritzing 0.8.7b)
breadboards: 1

parts:
  BeagleBone1 = BeagleBone Black
  IC1 = L293D [package=THT]
  M1 = Stepper Motor - Bipolar

nets:
  N1: BeagleBone1.no_name_yet#1, IC1.0V
  N2: BeagleBone1.no_name_yet#3, IC1.Enable_1, IC1.Enable_2, IC1.+V
  N3: BeagleBone1.no_name_yet#7, IC1.+Vmotor
  N4: BeagleBone1.no_name_yet#11, IC1.In_1
  N5: BeagleBone1.no_name_yet#13, IC1.In_2
  N6: BeagleBone1.no_name_yet#15, IC1.In_3
  N7: BeagleBone1.no_name_yet#17, IC1.In_4
  N8: IC1.Out_1_(_Controlled_by_Enable_1_), M1.B
  N9: IC1.Out_2_(_Controlled_by_Enable_1_), M1.D
  N10: IC1.Out_3_(_Controlled_by_Enable_2_), M1.A
  N11: IC1.Out_4_(_Controlled_by_Enable_2_), M1.C

notes:
  +
  -

custom parts:
  BeagleBone Black: BeagleBone Black rev. A5B
