# Fritzing sketch dcMotor (saved by Fritzing 0.8.7b)
breadboards: 1

parts:
  BeagleBone1 = BeagleBone Black
  R1 = Resistor [tolerance=±5% resistance=1k package=THT]
  M1 = DC Motor
  D1 = Diode [package=diode-1n4001]  # not connected
  Q2 = NPN-Transistor [package="SOT-23 [SMD]"]

nets:
  N1: BeagleBone1.no_name_yet#1, Q2.2
  N2: BeagleBone1.no_name_yet#3, M1.pin_2
  N3: BeagleBone1.no_name_yet#14, R1.Pin_1
  N4: R1.Pin_0, Q2.0
  N5: M1.pin_1, Q2.1

notes:
  +
  -
  P9
  P8

custom parts:
  BeagleBone Black: BeagleBone Black rev. A5B
