# Fritzing sketch h-bridgeMotorExternal (saved by Fritzing 0.8.7b)
breadboards: 1

parts:
  BeagleBone1 = BeagleBone Black
  IC1 = L293D [package=THT]
  M2 = DC Motor
  JACK1 = 2.1mm Barrel Jack with Terminal Block

nets:
  N1: BeagleBone1.no_name_yet#1, IC1.0V, JACK1.NEG
  N2: BeagleBone1.no_name_yet#3, IC1.+V
  N3: BeagleBone1.no_name_yet#15, IC1.In_3
  N4: BeagleBone1.no_name_yet#16, IC1.In_4
  N5: BeagleBone1.no_name_yet#21, IC1.Enable_2
  N6: IC1.+Vmotor, JACK1.POS
  N7: IC1.Out_3_(_Controlled_by_Enable_2_), M2.pin_2
  N8: IC1.Out_4_(_Controlled_by_Enable_2_), M2.pin_1

notes:
  +
  -

custom parts:
  BeagleBone Black: BeagleBone Black rev. A5B
