# Fritzing sketch h-bridgeMotorOLD (saved by Fritzing 0.8.7b)
breadboards: 1

parts:
  BeagleBone1 = BeagleBone Black
  IC1 = L293D [package=THT]
  M2 = DC Motor

nets:
  N1: BeagleBone1.no_name_yet#1, IC1.0V
  N2: BeagleBone1.no_name_yet#3, IC1.+Vmotor
  N3: BeagleBone1.no_name_yet#11, IC1.In_1
  N4: BeagleBone1.no_name_yet#13, IC1.In_2
  N5: BeagleBone1.no_name_yet#21, IC1.Enable_1
  N6: IC1.Out_1_(_Controlled_by_Enable_1_), M2.pin_1
  N7: IC1.Out_2_(_Controlled_by_Enable_1_), M2.pin_2

notes:
  +
  -

custom parts:
  BeagleBone Black: BeagleBone Black rev. A5B
