# Fritzing sketch unipolarStepperMotor (saved by Fritzing 0.8.7b)
breadboards: 1

parts:
  BeagleBone1 = BeagleBone Black
  IC1 = ULN2003A [package="SO16 [SMD]"]  # not connected
  M1 = Stepper Motor - Unipolar

nets:
  N1: BeagleBone1.no_name_yet#7, M1.COMMON_1, M1.COMMON_2

notes:
  +
  -
  P9
  P8

custom parts:
  BeagleBone Black: BeagleBone Black rev. A5B
