# Fritzing sketch servoMotor5V (saved by Fritzing 0.8.7b)
breadboards: 1

parts:
  BeagleBone1 = BeagleBone Black
  J1 = Basic Servo
  R1 = Resistor [tolerance=±5% resistance=1k package=THT]

nets:
  N1: BeagleBone1.no_name_yet#1, J1.gnd
  N2: BeagleBone1.no_name_yet#7, J1.vcc
  N3: BeagleBone1.no_name_yet#21, R1.Pin_1
  N4: J1.pulse, R1.Pin_0

notes:
  +
  -

custom parts:
  BeagleBone Black: BeagleBone Black rev. A5B
