# Fritzing sketch xbee (saved by Fritzing 0.8.7b)
breadboards: 1

parts:
  BeagleBone1 = BeagleBone Black
  xbee1 = Adafruit Xbee Adapter v1.1 [part_number=126]

nets:
  N1: BeagleBone1.no_name_yet#1, xbee1.gnd
  N2: BeagleBone1.no_name_yet#3, xbee1.3v#10
  N3: BeagleBone1.no_name_yet#24, xbee1.rx
  N4: BeagleBone1.no_name_yet#26, xbee1.tx

custom parts:
  BeagleBone Black: BeagleBone Black rev. A5B
  Adafruit Xbee Adapter v1.1: Adafruit Xbee Adapter
