# Fritzing sketch pushLEDmmap (saved by Fritzing 0.9.0b)
breadboards: 1

parts:
  BeagleBone1 = BeagleBone Black
  LED1 = LED - 5mm [color="Red (633nm)" package="5 mm [THT]"]
  R1 = Resistor [tolerance=±5% resistance=220 package=THT]
  S1 = Pushbutton [package="[THT]"]

nets:
  N1: BeagleBone1.no_name_yet#1, R1.Pin_1
  N2: BeagleBone1.no_name_yet#3, S1.Pin_1, S1.Pin_2
  N3: BeagleBone1.no_name_yet#15, LED1.anode
  N4: BeagleBone1.no_name_yet#42, S1.Pin_3, S1.Pin_4
  N5: LED1.cathode, R1.Pin_0

custom parts:
  BeagleBone Black: BeagleBone Black rev. A5B
