# Fritzing sketch quickBot5IR (saved by Fritzing 0.8.7b)
breadboards: 2

parts:
  BeagleBone1 = BeagleBone Black
  IC1 = L293D [package=THT]  # not connected
  JP1 = Header 3 [package=screwterminal-3.5mm-3_lock.007s]
  JP2 = Header 3 [package=screwterminal-3.5mm-3_lock.007s]
  J1 = Infrared Proximity Sensor
  J3 = Infrared Proximity Sensor
  J4 = Infrared Proximity Sensor
  J5 = Infrared Proximity Sensor
  J6 = Infrared Proximity Sensor
  R1 = Resistor [tolerance=±5% resistance=10k package=THT]
  R2 = Resistor [tolerance=±5% resistance=20k package=THT]
  R3 = Resistor [tolerance=±5% resistance=10k package=THT]
  R4 = Resistor [tolerance=±5% resistance=10k package=THT]
  R5 = Resistor [tolerance=±5% resistance=10k package=THT]
  R6 = Resistor [tolerance=±5% resistance=10k package=THT]
  R7 = Resistor [tolerance=±5% resistance=20k package=THT]
  R8 = Resistor [tolerance=±5% resistance=20k package=THT]
  R9 = Resistor [tolerance=±5% resistance=20k package=THT]
  R10 = Resistor [tolerance=±5% resistance=20k package=THT]
  R11 = Resistor [tolerance=±5% resistance=10k package=THT]
  R12 = Resistor [tolerance=±5% resistance=10k package=THT]
  R13 = Resistor [tolerance=±5% resistance=20k package=THT]
  R14 = Resistor [tolerance=±5% resistance=20k package=THT]

nets:
  N1: BeagleBone1.no_name_yet#1, J1.Vcc, R1.Pin_0, R3.Pin_0, R4.Pin_0, R5.Pin_0, R6.Pin_0, R11.Pin_0, R12.Pin_0
  N2: BeagleBone1.no_name_yet#33, R12.Pin_1, R14.Pin_0
  N3: BeagleBone1.no_name_yet#35, R11.Pin_1, R13.Pin_0
  N4: BeagleBone1.no_name_yet#36, R1.Pin_1, R2.Pin_0
  N5: BeagleBone1.no_name_yet#37, R6.Pin_1, R10.Pin_0
  N6: BeagleBone1.no_name_yet#38, R3.Pin_1, R7.Pin_0
  N7: BeagleBone1.no_name_yet#39, R5.Pin_1, R9.Pin_0
  N8: BeagleBone1.no_name_yet#40, R4.Pin_1, R8.Pin_0
  N9: JP1.1, R9.Pin_1
  N10: JP2.1, R10.Pin_1
  N11: J1.Vout, R7.Pin_1
  N12: J3.Vout, R14.Pin_1
  N13: J4.Vout, R2.Pin_1
  N14: J5.Vout, R8.Pin_1
  N15: J6.Vout, R13.Pin_1

notes:
  +
  -
  P9
  P8

custom parts:
  BeagleBone Black: BeagleBone Black rev. A5B
