# Fritzing sketch quickBot_play (saved by Fritzing 0.9.0b)
circuit board: 5.461cm x 8.636cm
breadboards: 2

parts:
  IC1 = L293D [package=THT]
  JP1 = Header 3 [package=screwterminal-3.5mm-3_lock.007s]
  JP2 = Header 3 [package=screwterminal-3.5mm-3_lock.007s]
  J4 = Infrared Proximity Sensor
  R1 = Resistor [tolerance=±5% resistance=1 package=THT]
  R2 = Resistor [tolerance=±5% resistance=20k package=THT]
  R5 = Resistor [tolerance=±5% resistance=10k package=THT]
  R6 = Resistor [tolerance=±5% resistance=10k package=THT]
  R10 = Resistor [tolerance=±5% resistance=20k package=THT]
  R9 = Resistor [tolerance=±5% resistance=20k package=THT]
  M1 = DC Motor
  M2 = DC Motor
  JACK2 = 2.1mm Barrel Jack with Terminal Block
  BeagleBone1 = BeagleBone Black

nets:
  N1: IC1.Enable_1, BeagleBone1.no_name_yet#14
  N2: IC1.In_1, BeagleBone1.no_name_yet#109
  N3: IC1.Out_1_(_Controlled_by_Enable_1_), M2.pin_2
  N4: IC1.0V, JP1.2, JP2.2, J4.GND, R1.Pin_0, R5.Pin_0, R6.Pin_0, JACK2.NEG, BeagleBone1.no_name_yet#2
  N5: IC1.Out_2_(_Controlled_by_Enable_1_), M2.pin_1
  N6: IC1.In_2, BeagleBone1.no_name_yet#111
  N7: IC1.+Vmotor, JACK2.POS
  N8: IC1.Enable_2, BeagleBone1.no_name_yet#16
  N9: IC1.In_3, BeagleBone1.no_name_yet#115
  N10: IC1.Out_3_(_Controlled_by_Enable_2_), M1.pin_2
  N11: IC1.Out_4_(_Controlled_by_Enable_2_), M1.pin_1
  N12: IC1.In_4, BeagleBone1.no_name_yet#113
  N13: IC1.+V, JP1.3, JP2.3, J4.Vcc, BeagleBone1.no_name_yet#4
  N14: JP1.1, R9.Pin_1
  N15: JP2.1, R10.Pin_1
  N16: J4.Vout, R2.Pin_1
  N17: R1.Pin_1, R2.Pin_0, BeagleBone1.no_name_yet#36
  N18: R5.Pin_1, R9.Pin_0, BeagleBone1.no_name_yet#40
  N19: R6.Pin_1, R10.Pin_0, BeagleBone1.no_name_yet#38

notes:
  +
  -
  P9
  P8
  beagleboard.org/cookbook

custom parts:
  BeagleBone Black: BeagleBone Black rev. A5B
