# Fritzing sketch roboCape (saved by Fritzing 0.8.7b)
circuit board: 5.588cm x 8.77711cm
breadboards: 1

parts:
  BeagleBone1 = BeagleBone Black
  J1 = Infrared Proximity Sensor

nets:
  N1: BeagleBone1.no_name_yet#2, J1.Vcc
  N2: BeagleBone1.no_name_yet#4, J1.Vout
  N3: BeagleBone1.no_name_yet#34, J1.GND

notes:
  +
  -
  P9
  P8

custom parts:
  BeagleBone Black: BeagleBone Black rev. A5B
